# Fritzing sketch phtemp (saved by Fritzing 0.9.2b)
breadboards: 1

parts:
  Part1 = Arduino Nano (Rev3.0)
  pH_Circuit1 = pH Circuit
  Pre-Assembled_Female_BNC1 = Pre-Assembled Female BNC
  Conductivity_Circuit1 = Conductivity Circuit
  Pre-Assembled_Female_BNC2 = Pre-Assembled Female BNC
  NRF24L1 = NRF24L01

nets:
  GND: Part1.GND, pH_Circuit1.GND#0, Conductivity_Circuit1.GND#0, NRF24L1.GND
  N1: Part1.D9, NRF24L1.CE
  N2: Part1.D10, NRF24L1.CSN
  N3: Part1.D11/MOSI, NRF24L1.MOSI
  N4: Part1.D12/MISO, NRF24L1.MISO
  VCC: Part1.3V3, pH_Circuit1.Vcc, Conductivity_Circuit1.Vcc, NRF24L1.VCC
  N5: Part1.D13/SCK, NRF24L1.SCK
  N6: pH_Circuit1.TX, Conductivity_Circuit1.TX
  N7: pH_Circuit1.RX, Conductivity_Circuit1.RX
  N8: pH_Circuit1.PRB, Pre-Assembled_Female_BNC1.PRB
  N9: pH_Circuit1.GND#5, Pre-Assembled_Female_BNC1.GND
  N10: Conductivity_Circuit1.PRB, Pre-Assembled_Female_BNC2.PRB
  N11: Conductivity_Circuit1.GND#5, Pre-Assembled_Female_BNC2.GND

custom parts:
  NRF24L01: NRF24L01 module
